// Logisim project jiaotongxinhaodeng.circ as structural Verilog: 6 circuits, main circuit main
module main (
  input  night,
  input  emergency,
  input  reset,
  input  normal_load
);

  wire and_3_out, and_4_out, and_5_out, and_6_out, and_7_out, and_8_out, and_9_out, and_10_out, clk,
       emergency_t, EWgreen, EWred, EWyellow, night_t, not_1_out, not_2_out, not_3_out, not_4_out, not_5_out,
       not_6_out, not_7_out, not_8_out, not_9_out, not_10_out, not_11_out, not_12_out, not_13_out,
       not_14_out, not_15_out, NSgreen, NSred, NSyellow, or_1_out, or_2_out, or_3_out, or_4_out;
  wire [3:0] and_11_out, and_12_out, and_13_out, and_14_out, emergency4, EWgewei, EWshiwei, night4,
       not_16_out, not_17_out, not_18_out, not_19_out, not_20_out, not_21_out, not_22_out, not_23_out,
       NSgewei, NSshiwei, zhuangtaifenpei_1_geweizongxian, zhuangtaifenpei_1_gezongxian40,
       zhuangtaifenpei_1_shiweizongxian, zhuangtaifenpei_1_shizongxian40;

  not not_1 (not_1_out, reset);
  Clock u_clk (.out(clk));
  not not_2 (not_2_out, emergency_t);
  not not_3 (not_3_out, night_t);
  not not_4 (not_4_out, emergency_t);
  and and_1 (night_t, night, not_1_out);
  and and_2 (emergency_t, emergency, not_1_out);
  and and_3 (and_3_out, NSyellow, not_2_out, not_3_out);
  and and_4 (and_4_out, not_4_out, night_t, clk);
  not not_5 (not_5_out, emergency_t);
  not not_6 (not_6_out, night_t);
  not not_7 (not_7_out, emergency_t);
  not not_8 (not_8_out, night_t);
  and and_5 (and_5_out, NSred, not_8_out, not_9_out);
  not not_9 (not_9_out, emergency_t);
  or or_1 (or_1_out, and_3_out, and_4_out);
  and and_6 (and_6_out, EWyellow, not_5_out, not_6_out);
  and and_7 (and_7_out, not_7_out, night_t, clk);
  or or_2 (or_2_out, emergency_t, and_5_out);
  not not_10 (not_10_out, night_t);
  not not_11 (not_11_out, emergency_t);
  not not_12 (not_12_out, night_t);
  and and_8 (and_8_out, EWred, not_12_out, not_13_out);
  not not_13 (not_13_out, emergency_t);
  not not_14 (not_14_out, night_t);
  not not_15 (not_15_out, emergency_t);
  or or_3 (or_3_out, and_6_out, and_7_out);
  assign emergency4 = {{3{emergency_t}}, emergency_t};  // Bit_Extender bit_extender_1
  assign night4 = {{3{night_t}}, night_t};  // Bit_Extender bit_extender_2
  LED u_NSred (.in(or_2_out));
  and and_9 (and_9_out, NSgreen, not_10_out, not_11_out);
  LED u_NSgreen (.in(and_9_out));
  LED u_NSyellow (.in(or_1_out));
  or or_4 (or_4_out, emergency_t, and_8_out);
  LED u_EWred (.in(or_4_out));
  and and_10 (and_10_out, EWgreen, not_14_out, not_15_out);
  LED u_EWgreen (.in(and_10_out));
  LED u_EWyellow (.in(or_3_out));
  zhuangtaifenpei zhuangtaifenpei_1 (
    .Reset(reset), .load(normal_load), .CLK(clk), .EWred(EWred), .EWgreen(EWgreen), .EWyellow(EWyellow),
    .NSred(NSred), .NSgreen(NSgreen), .NSyellow(NSyellow), .gezongxian40(zhuangtaifenpei_1_gezongxian40),
    .shizongxian40(zhuangtaifenpei_1_shizongxian40), .geweizongxian(zhuangtaifenpei_1_geweizongxian),
    .shiweizongxian(zhuangtaifenpei_1_shiweizongxian));
  assign not_16_out = ~emergency4;  // NOT_Gate not_16, 4 bits wide
  assign not_17_out = ~night4;  // NOT_Gate not_17, 4 bits wide
  assign not_18_out = ~emergency4;  // NOT_Gate not_18, 4 bits wide
  assign not_19_out = ~night4;  // NOT_Gate not_19, 4 bits wide
  assign not_20_out = ~emergency4;  // NOT_Gate not_20, 4 bits wide
  assign not_21_out = ~night4;  // NOT_Gate not_21, 4 bits wide
  assign not_22_out = ~emergency4;  // NOT_Gate not_22, 4 bits wide
  assign not_23_out = ~night4;  // NOT_Gate not_23, 4 bits wide
  assign and_11_out = not_16_out & not_17_out & NSshiwei;  // AND_Gate and_11, 4 bits wide
  assign and_12_out = not_18_out & not_19_out & NSgewei;  // AND_Gate and_12, 4 bits wide
  assign and_13_out = not_20_out & not_21_out & EWshiwei;  // AND_Gate and_13, 4 bits wide
  assign and_14_out = not_22_out & not_23_out & EWgewei;  // AND_Gate and_14, 4 bits wide
  jishuqiyima jishuqiyima_1 (
    .Red(EWred), .Green(EWgreen), .Yellow(EWyellow), .shiwei40s(zhuangtaifenpei_1_shizongxian40),
    .gewei40s(zhuangtaifenpei_1_gezongxian40), .shiwei35_5s(zhuangtaifenpei_1_shiweizongxian),
    .gewei35_5s(zhuangtaifenpei_1_geweizongxian), .shiwei(EWshiwei), .gewei(EWgewei));
  jishuqiyima jishuqiyima_2 (
    .Red(NSred), .Green(NSgreen), .Yellow(NSyellow), .shiwei40s(zhuangtaifenpei_1_shizongxian40),
    .gewei40s(zhuangtaifenpei_1_gezongxian40), .shiwei35_5s(zhuangtaifenpei_1_shiweizongxian),
    .gewei35_5s(zhuangtaifenpei_1_geweizongxian), .shiwei(NSshiwei), .gewei(NSgewei));
  Hex_Digit_Display u_NSshiwei (.value(and_11_out));  // open: dp
  Hex_Digit_Display u_EWshiwei (.value(and_13_out));  // open: dp
  Hex_Digit_Display u_NSgewei (.value(and_12_out));  // open: dp
  Hex_Digit_Display u_EWgewei (.value(and_14_out));  // open: dp
endmodule

module daojishi35s (
  input  load,
  input  clk,
  output done,
  output [3:0] ge,
  output [3:0] ten
);

  wire shiwei_pin1, shiwei_pin4, shiwei_pin10, shiwei_pin13;

  _74192 #(.ShowInternalStructure("true")) shiwei (
    .pin1(shiwei_pin1), .pin2(ten[1]), .pin3(ten[0]), .pin4(shiwei_pin4), .pin5(shiwei_pin1), .pin6(ten[2]),
    .pin7(ten[3]), .pin15(shiwei_pin1), .pin13(shiwei_pin13), .pin11(load), .pin10(shiwei_pin10),
    .pin9(shiwei_pin10));  // open: pin14, pin12
  _74192 #(.ShowInternalStructure("true")) gewei (
    .pin1(shiwei_pin10), .pin2(ge[1]), .pin3(ge[0]), .pin4(clk), .pin5(shiwei_pin1), .pin6(ge[2]),
    .pin7(ge[3]), .pin15(shiwei_pin1), .pin13(shiwei_pin4), .pin11(load), .pin10(shiwei_pin1),
    .pin9(shiwei_pin10));  // open: pin14, pin12
  not not_1 (done, shiwei_pin13);
  // also tied to GND on the sheet: shiwei_pin10
  // also tied to VCC on the sheet: shiwei_pin1
endmodule

module daojishi5s (
  input  load,
  input  clk,
  output done,
  output [3:0] ge
);

  wire n74192_1_pin1, n74192_1_pin5, n74192_1_pin13;

  _74192 #(.ShowInternalStructure("true")) u_74192_1 (
    .pin1(n74192_1_pin1), .pin2(ge[1]), .pin3(ge[0]), .pin4(clk), .pin5(n74192_1_pin5), .pin6(ge[2]),
    .pin7(ge[3]), .pin15(n74192_1_pin1), .pin13(n74192_1_pin13), .pin11(load), .pin10(n74192_1_pin5),
    .pin9(n74192_1_pin1));  // open: pin14, pin12
  not not_1 (done, n74192_1_pin13);
  // also tied to GND on the sheet: n74192_1_pin1
  // also tied to VCC on the sheet: n74192_1_pin5
endmodule

module zhuangtaifenpei (
  input  Reset,
  input  load,
  input  CLK,
  output EWred,
  output EWgreen,
  output EWyellow,
  output NSred,
  output NSgreen,
  output NSyellow,
  output [3:0] gezongxian40,
  output [3:0] shizongxian40,
  output [3:0] geweizongxian,
  output [3:0] shiweizongxian
);

  wire and_1_out, and_2_out, and_3_out, and_4_out, and_5_out, and_25_out, and_26_out, and_27_out,
       daojishi5s_1_done, daojishi5s_2_done, daojishi35s_1_done, daojishi35s_2_done, daojishi40s_1_done,
       ge00, ge01, ge02, ge03, ge10, ge11, ge12, ge13, ge20, ge21, ge22, ge23, ge30, ge31, ge32, ge33,
       load_40_1, load_40_2, nand_1_out, not_2_out, not_4_out, not_5_out, not_6_out, not_7_out, not_8_out,
       not_9_out, not_10_out, not_11_out, or_5_out, or_6_out, Q0, Q1, S00, S01, S02, S03, S20, S21, S22, S23,
       xor_1_out, xor_2_out;
  wire [3:0] S0gewei, S0shiwei, S1gewei, S2gewei, S2shiwei, S3gewei;

  nor nor_1 (load_40_1, Reset, and_5_out, load);
  nand nand_1 (nand_1_out, not_11_out, CLK);
  // NOT_Gate not_1 has open pins: in=daojishi40s_1_done, out=open
  and and_1 (and_1_out, load_40_1, load_40_2);
  not not_2 (not_2_out, and_2_out);
  not not_3 (load_40_2, and_3_out);
  not not_4 (not_4_out, and_4_out);
  or or_1 (shiweizongxian[1], S01, S21);
  or or_2 (shiweizongxian[2], S02, S22);
  or or_3 (shiweizongxian[3], S03, S23);
  daojishi35s daojishi35s_1 (
    .load(load_40_1), .clk(nand_1_out), .done(daojishi35s_1_done), .ge(S0gewei), .ten(S0shiwei));
  daojishi5s daojishi5s_1 (.load(not_2_out), .clk(nand_1_out), .done(daojishi5s_1_done), .ge(S1gewei));
  daojishi35s daojishi35s_2 (
    .load(load_40_2), .clk(nand_1_out), .done(daojishi35s_2_done), .ge(S2gewei), .ten(S2shiwei));
  daojishi5s daojishi5s_2 (.load(not_4_out), .clk(nand_1_out), .done(daojishi5s_2_done), .ge(S3gewei));
  or or_4 (shiweizongxian[0], S00, S20);
  not not_5 (not_5_out, Q1);
  not not_6 (not_6_out, Q0);
  daojishi40s daojishi40s_1 (
    .load(and_1_out), .clk(nand_1_out), .done(daojishi40s_1_done), .ge(gezongxian40), .ten(shizongxian40));
  not not_7 (not_7_out, Q1);
  and and_2 (and_2_out, daojishi35s_1_done, not_7_out, not_8_out);
  not not_8 (not_8_out, Q0);
  not not_9 (not_9_out, Q1);
  and and_3 (and_3_out, daojishi5s_1_done, not_9_out, Q0);
  and and_4 (and_4_out, daojishi35s_2_done, Q1, not_10_out);
  not not_10 (not_10_out, Q0);
  and and_5 (and_5_out, daojishi5s_2_done, Q1, Q0);
  nor nor_2 (EWgreen, Q1, Q0);
  and and_6 (EWyellow, not_5_out, Q0);
  and and_7 (NSgreen, Q1, not_6_out);
  and and_8 (NSyellow, Q1, Q0);
  and and_9 (ge00, EWgreen, S0gewei[0]);
  and and_10 (ge10, EWgreen, S0gewei[1]);
  and and_11 (ge20, EWgreen, S0gewei[2]);
  and and_12 (ge30, EWgreen, S0gewei[3]);
  and and_13 (ge02, NSgreen, S2gewei[0]);
  and and_14 (ge12, NSgreen, S2gewei[1]);
  and and_15 (ge22, NSgreen, S2gewei[2]);
  and and_16 (ge32, NSgreen, S2gewei[3]);
  and and_17 (S00, EWgreen, S0shiwei[0]);
  and and_18 (S01, EWgreen, S0shiwei[1]);
  and and_19 (S02, EWgreen, S0shiwei[2]);
  and and_20 (S03, EWgreen, S0shiwei[3]);
  and and_21 (S20, NSgreen, S2shiwei[0]);
  and and_22 (S21, NSgreen, S2shiwei[1]);
  and and_23 (S22, NSgreen, S2shiwei[2]);
  and and_24 (S23, NSgreen, S2shiwei[3]);
  or or_5 (or_5_out, and_2_out, and_3_out, and_4_out, and_5_out);
  or or_6 (or_6_out, and_2_out, and_3_out, and_4_out, and_5_out);
  not not_11 (not_11_out, Reset);
  xor xor_1 (xor_1_out, Q1, and_25_out);
  and and_25 (and_25_out, or_5_out, Q0);
  xor xor_2 (xor_2_out, Q0, or_6_out);
  or or_7 (EWred, NSyellow, NSgreen);
  or or_8 (NSred, EWgreen, EWyellow);
  D_Flip_Flop DQ1 (.D(and_26_out), .clk(nand_1_out), .Q(Q1));  // open: Qn, preset, reset
  and and_26 (and_26_out, xor_1_out, not_11_out);
  D_Flip_Flop DQ0 (.D(and_27_out), .clk(nand_1_out), .Q(Q0));  // open: Qn, preset, reset
  and and_27 (and_27_out, xor_2_out, not_11_out);
  or or_9 (geweizongxian[1], ge10, ge11, ge12, ge13);
  and and_28 (ge01, EWyellow, S1gewei[0]);
  and and_29 (ge11, EWyellow, S1gewei[1]);
  and and_30 (ge21, EWyellow, S1gewei[2]);
  and and_31 (ge31, EWyellow, S1gewei[3]);
  and and_32 (ge03, NSyellow, S3gewei[0]);
  and and_33 (ge13, NSyellow, S3gewei[1]);
  and and_34 (ge23, NSyellow, S3gewei[2]);
  and and_35 (ge33, NSyellow, S3gewei[3]);
  or or_10 (geweizongxian[0], ge00, ge01, ge02, ge03);
  or or_11 (geweizongxian[2], ge22, ge20, ge21, ge23);
  or or_12 (geweizongxian[3], ge30, ge31, ge32, ge33);

  // Other names for the same wires on the sheet: S0 = EWgreen; S1 = EWyellow; S2 = NSgreen; S3 = NSyellow
endmodule

module daojishi40s (
  input  load,
  input  clk,
  output done,
  output [3:0] ge,
  output [3:0] ten
);

  wire gewei_pin13, n7414_1_pin12, shiwei_pin1, shiwei_pin4, shiwei_pin5, shiwei_pin13;

  _74192 #(.ShowInternalStructure("true")) shiwei (
    .pin1(shiwei_pin1), .pin2(ten[1]), .pin3(ten[0]), .pin4(shiwei_pin4), .pin5(shiwei_pin5), .pin6(ten[2]),
    .pin7(ten[3]), .pin15(shiwei_pin1), .pin13(shiwei_pin13), .pin11(load), .pin10(shiwei_pin5),
    .pin9(shiwei_pin1));  // open: pin14, pin12
  Pull_Resistor #(.pull(1)) pull_resistor_1 (.node(shiwei_pin5));
  _74192 #(.ShowInternalStructure("true")) gewei (
    .pin1(shiwei_pin1), .pin2(ge[1]), .pin3(ge[0]), .pin4(clk), .pin5(shiwei_pin5), .pin6(ge[2]),
    .pin7(ge[3]), .pin15(shiwei_pin1), .pin13(gewei_pin13), .pin11(load), .pin10(shiwei_pin1),
    .pin9(shiwei_pin1));  // open: pin14, pin12
  not not_1 (done, shiwei_pin13);
  _7414 #(.ShowInternalStructure("true")) u_7414_1 (
    .pin13(gewei_pin13), .pin12(n7414_1_pin12), .pin11(n7414_1_pin12), .pin10(shiwei_pin4));  // open: pin1, pin2, pin3, pin4, pin5, pin6, pin9, pin8
  // also tied to GND on the sheet: shiwei_pin1
  // also tied to VCC on the sheet: shiwei_pin5
endmodule

module jishuqiyima (
  input  Red,
  input  Green,
  input  Yellow,
  input  [3:0] shiwei40s,
  input  [3:0] gewei40s,
  input  [3:0] shiwei35_5s,
  input  [3:0] gewei35_5s,
  output [3:0] shiwei,
  output [3:0] gewei
);

  wire GY;
  wire [3:0] and_1_out, and_2_out, and_3_out, and_4_out, bit_extender_1_out, bit_extender_2_out,
       bit_extender_3_out, bit_extender_4_out;

  or or_1 (GY, Green, Yellow);
  assign bit_extender_1_out = {{3{Red}}, Red};  // Bit_Extender bit_extender_1
  assign bit_extender_2_out = {{3{Red}}, Red};  // Bit_Extender bit_extender_2
  assign bit_extender_3_out = {{3{GY}}, GY};  // Bit_Extender bit_extender_3
  assign bit_extender_4_out = {{3{GY}}, GY};  // Bit_Extender bit_extender_4
  assign and_1_out = shiwei40s & bit_extender_1_out;  // AND_Gate and_1, 4 bits wide
  assign and_2_out = gewei40s & bit_extender_2_out;  // AND_Gate and_2, 4 bits wide
  assign and_3_out = shiwei35_5s & bit_extender_3_out;  // AND_Gate and_3, 4 bits wide
  assign and_4_out = gewei35_5s & bit_extender_4_out;  // AND_Gate and_4, 4 bits wide
  assign shiwei = and_1_out | and_3_out;  // OR_Gate or_2, 4 bits wide
  assign gewei = and_2_out | and_4_out;  // OR_Gate or_3, 4 bits wide

  // Other names for the same wires on the sheet: R = Red
endmodule
